// Logisim project single_cycle_shifter.circ as structural Verilog: 1 circuit, main circuit single_cycle_shifter
module single_cycle_shifter (
  input  in_1,
  input  [2:0] in_2,
  input  [31:0] in_3,
  input  [4:0] in_4,
  output [31:0] out_5
);

  wire and_1_out, and_4_out, and_5_out, and_6_out, and_7_out, and_10_out, and_11_out, and_15_out, and_16_out,
       and_20_out, and_21_out, not_2_out, not_3_out, not_4_out, not_5_out, not_6_out, not_7_out, not_8_out,
       not_9_out, not_10_out, not_11_out, shift_to_left, shift_to_right;
  wire [0:0] controlled_buffer_1_out;
  wire [31:0] controlled_buffer_1_out_2, controlled_buffer_6_out, controlled_buffer_8_out,
       controlled_buffer_9_out, controlled_buffer_13_out, controlled_buffer_16_out, controlled_buffer_18_out,
       controlled_buffer_21_out, controlled_buffer_23_out, controlled_buffer_26_out;
  wire [31:2] controlled_buffer_3_out;
  wire [31:28] controlled_buffer_3_out_2;
  wire [31:31] and_2_out, and_9_out, and_12_out, and_13_out, and_14_out, and_17_out, and_18_out, and_19_out;

  // NOT_Gate not_1 is placed but not wired
  // Probe on in_3
  assign {controlled_buffer_1_out_2[30:0], controlled_buffer_1_out[0]} = shift_to_left ? {in_3[0], in_3[1], in_3[2], in_3[3], in_3[4], in_3[5], in_3[6], in_3[7], in_3[8], in_3[9], in_3[10], in_3[11], in_3[12], in_3[13], in_3[14], in_3[15], in_3[16], in_3[17], in_3[18], in_3[19], in_3[20], in_3[21], in_3[22], in_3[23], in_3[24], in_3[25], in_3[26], in_3[27], in_3[28], in_3[29], in_3[30], in_3[31]} : 32'bz;  // Controlled_Buffer controlled_buffer_1
  assign {controlled_buffer_1_out_2[30:0], controlled_buffer_1_out[0]} = shift_to_right ? in_3 : 32'bz;  // Controlled_Buffer controlled_buffer_2
  // Probe on {controlled_buffer_1_out_2[30:0], controlled_buffer_1_out[0]}
  and and_1 (and_1_out, shift_to_right, in_1);
  assign {controlled_buffer_3_out_2[29:28], controlled_buffer_3_out} = not_2_out ? in_3 : 32'bz;  // Controlled_Buffer controlled_buffer_3
  not not_2 (not_2_out, in_4[0]);
  and and_2 (and_2_out[31], in_3[31], in_1);
  not not_3 (not_3_out, in_4[0]);
  and and_3 (controlled_buffer_1_out_2[31], controlled_buffer_1_out_2[30], and_1_out);
  assign {controlled_buffer_3_out_2[29:28], controlled_buffer_3_out} = and_4_out ? {in_3[30:0], 1'b0} : 32'bz;  // Controlled_Buffer controlled_buffer_4
  and and_4 (and_4_out, shift_to_left, in_4[0]);
  and and_5 (and_5_out, shift_to_right, in_4[0]);
  assign {controlled_buffer_3_out_2[29:28], controlled_buffer_3_out} = and_5_out ? {and_2_out[31], in_3[31:1]} : 32'bz;  // Controlled_Buffer controlled_buffer_5
  // Probe on controlled_buffer_6_out
  assign controlled_buffer_6_out = not_3_out ? {controlled_buffer_1_out_2[30:0], controlled_buffer_1_out[0]} : 32'bz;  // Controlled_Buffer controlled_buffer_6
  assign controlled_buffer_6_out = in_4[0] ? controlled_buffer_1_out_2 : 32'bz;  // Controlled_Buffer controlled_buffer_7
  and and_6 (and_6_out, shift_to_left, in_4[1]);
  assign controlled_buffer_8_out = not_4_out ? {controlled_buffer_3_out_2[29:28], controlled_buffer_3_out} : 32'bz;  // Controlled_Buffer controlled_buffer_8
  not not_4 (not_4_out, in_4[1]);
  and and_7 (and_7_out, shift_to_right, in_4[1]);
  and and_8 (controlled_buffer_3_out_2[31], controlled_buffer_3_out_2[29], in_1);
  Decoder #(.enable("false"), .select(3)) decoder_1 (
    .out1(shift_to_left), .out5(shift_to_right), .sel(in_2));  // open: out0, out2, out3, out4, out6, out7
  assign controlled_buffer_9_out = not_5_out ? controlled_buffer_6_out : 32'bz;  // Controlled_Buffer controlled_buffer_9
  not not_5 (not_5_out, in_4[1]);
  assign controlled_buffer_9_out = in_4[1] ? {{2{and_9_out[31]}}, controlled_buffer_6_out[31:2]} : 32'bz;  // Controlled_Buffer controlled_buffer_10
  and and_9 (and_9_out[31], controlled_buffer_6_out[31], and_1_out);
  assign controlled_buffer_8_out = and_6_out ? {controlled_buffer_3_out, 2'b00} : 32'bz;  // Controlled_Buffer controlled_buffer_11
  assign controlled_buffer_8_out = and_7_out ? {{2{controlled_buffer_3_out_2[31]}}, controlled_buffer_3_out_2[29:28], controlled_buffer_3_out[31:4]} : 32'bz;  // Controlled_Buffer controlled_buffer_12
  // Probe on controlled_buffer_9_out
  assign controlled_buffer_13_out = and_10_out ? {controlled_buffer_8_out[27:0], 4'b0000} : 32'bz;  // Controlled_Buffer controlled_buffer_13
  and and_10 (and_10_out, shift_to_left, in_4[2]);
  assign controlled_buffer_13_out = not_6_out ? controlled_buffer_8_out : 32'bz;  // Controlled_Buffer controlled_buffer_14
  not not_6 (not_6_out, in_4[2]);
  and and_11 (and_11_out, shift_to_right, in_4[2]);
  assign controlled_buffer_13_out = and_11_out ? {{4{and_12_out[31]}}, controlled_buffer_8_out[31:4]} : 32'bz;  // Controlled_Buffer controlled_buffer_15
  and and_12 (and_12_out[31], controlled_buffer_8_out[31], in_1);
  // Probe on controlled_buffer_16_out
  assign controlled_buffer_16_out = not_7_out ? controlled_buffer_9_out : 32'bz;  // Controlled_Buffer controlled_buffer_16
  not not_7 (not_7_out, in_4[2]);
  assign controlled_buffer_16_out = in_4[2] ? {{4{and_13_out[31]}}, controlled_buffer_9_out[31:4]} : 32'bz;  // Controlled_Buffer controlled_buffer_17
  and and_13 (and_13_out[31], controlled_buffer_9_out[31], and_1_out);
  not not_8 (not_8_out, in_4[3]);
  and and_14 (and_14_out[31], controlled_buffer_16_out[31], and_1_out);
  assign controlled_buffer_18_out = and_15_out ? {controlled_buffer_13_out[23:0], {8{1'b0}}} : 32'bz;  // Controlled_Buffer controlled_buffer_18
  and and_15 (and_15_out, shift_to_left, in_4[3]);
  assign controlled_buffer_18_out = not_8_out ? controlled_buffer_13_out : 32'bz;  // Controlled_Buffer controlled_buffer_19
  and and_16 (and_16_out, shift_to_right, in_4[3]);
  assign controlled_buffer_18_out = and_16_out ? {{8{and_17_out[31]}}, controlled_buffer_13_out[31:8]} : 32'bz;  // Controlled_Buffer controlled_buffer_20
  and and_17 (and_17_out[31], controlled_buffer_13_out[31], in_1);
  // Probe on controlled_buffer_21_out
  assign controlled_buffer_21_out = not_9_out ? controlled_buffer_16_out : 32'bz;  // Controlled_Buffer controlled_buffer_21
  not not_9 (not_9_out, in_4[3]);
  assign controlled_buffer_21_out = in_4[3] ? {{8{and_14_out[31]}}, controlled_buffer_16_out[31:8]} : 32'bz;  // Controlled_Buffer controlled_buffer_22
  assign controlled_buffer_23_out = not_10_out ? controlled_buffer_18_out : 32'bz;  // Controlled_Buffer controlled_buffer_23
  not not_10 (not_10_out, in_4[4]);
  and and_18 (and_18_out[31], controlled_buffer_18_out[31], in_1);
  and and_19 (and_19_out[31], controlled_buffer_21_out[31], and_1_out);
  assign controlled_buffer_23_out = and_20_out ? {controlled_buffer_18_out[15:0], {16{1'b0}}} : 32'bz;  // Controlled_Buffer controlled_buffer_24
  and and_20 (and_20_out, shift_to_left, in_4[4]);
  and and_21 (and_21_out, shift_to_right, in_4[4]);
  assign controlled_buffer_23_out = and_21_out ? {{16{and_18_out[31]}}, controlled_buffer_18_out[31:16]} : 32'bz;  // Controlled_Buffer controlled_buffer_25
  // Probe on controlled_buffer_26_out
  assign controlled_buffer_26_out = not_11_out ? controlled_buffer_21_out : 32'bz;  // Controlled_Buffer controlled_buffer_26
  not not_11 (not_11_out, in_4[4]);
  assign controlled_buffer_26_out = in_4[4] ? {{16{and_19_out[31]}}, controlled_buffer_21_out[31:16]} : 32'bz;  // Controlled_Buffer controlled_buffer_27
  // Probe on controlled_buffer_23_out
  // Probe on out_5
  assign out_5 = shift_to_left ? {controlled_buffer_26_out[0], controlled_buffer_26_out[1], controlled_buffer_26_out[2], controlled_buffer_26_out[3], controlled_buffer_26_out[4], controlled_buffer_26_out[5], controlled_buffer_26_out[6], controlled_buffer_26_out[7], controlled_buffer_26_out[8], controlled_buffer_26_out[9], controlled_buffer_26_out[10], controlled_buffer_26_out[11], controlled_buffer_26_out[12], controlled_buffer_26_out[13], controlled_buffer_26_out[14], controlled_buffer_26_out[15], controlled_buffer_26_out[16], controlled_buffer_26_out[17], controlled_buffer_26_out[18], controlled_buffer_26_out[19], controlled_buffer_26_out[20], controlled_buffer_26_out[21], controlled_buffer_26_out[22], controlled_buffer_26_out[23], controlled_buffer_26_out[24], controlled_buffer_26_out[25], controlled_buffer_26_out[26], controlled_buffer_26_out[27], controlled_buffer_26_out[28], controlled_buffer_26_out[29], controlled_buffer_26_out[30], controlled_buffer_26_out[31]} : 32'bz;  // Controlled_Buffer controlled_buffer_28
  assign out_5 = shift_to_right ? controlled_buffer_26_out : 32'bz;  // Controlled_Buffer controlled_buffer_29
  // NOT_Gate not_12 is placed but not wired

  // Other names for the same wires on the sheet: input_data[31:0] = in_3; funct3[2:0] = in_2; is_arithmetic = in_1;
  //   shift_by[4:0] = in_4; shifted_data[31:0] = out_5

  // Notes on the sheet:
  //   Input reverse
  //   (if shifting to left)
  //   Not sure if this gate is needed as the "i" should never be "1" in left shift
  //   Inputs
  //   i: 31st bit of ins
  //   input data (from RB0)
  //   shift by (from RB1)
  //   | ins | func3 | i |
  //   | SLL | 001 | x |
  //   | SRL | 101 | 0 |
  //   | SRA | 101 | 1 |
  //   funct3
  //   Old design (more expensive, harder to route - probably)
  //   Outputs
  //   Output reverse
  //   (if shifting to left)
endmodule
